# Fritzing sketch project (saved by Fritzing 0.9.3b)
circuit board: 8.46667cm x 5.64444cm
breadboards: 1

parts:
  DIN1 = DIN-5 jack (MIDI) [package=THT]
  Part1 = Arduino Nano (Rev3.0)
  J1 = Power Jack [package=power_jack_pth_lock]
  Q3 = Basic FET N-Channel [part_number=NTD4809N-1G package="TO220 [THT]"]
  Q2 = Basic FET N-Channel [part_number=NTD4809N-1G package="TO220 [THT]"]
  Q1 = Basic FET N-Channel [part_number=NTD4809N-1G package="TO220 [THT]"]

nets:
  N1: DIN1.3, Q3.drain
  N2: DIN1.2, Q2.drain
  N3: DIN1.4, Part1.VIN, J1.PWR
  N4: DIN1.1, Q1.drain
  GND: Part1.GND, J1.GND, Q3.source, Q2.source, Q1.source
  N5: Part1.D3, Q3.gate
  N6: Part1.D5, Q2.gate
  N7: Part1.D6, Q1.gate

notes:
  12V 1A Center Positive
  Racing Ring Lighting Controller, 1.0
